# Fritzing sketch Schema (saved by Fritzing 0.8.7b)
breadboards: 1

parts:
  Parte1 = Arduino Mega 2560 (Rev3)
  IC1 = ULN2803A [package=THT]
  12V_External_Source = Power plug
  12V = LEDs [package=fkit-led-1206]
  12V_2 = LEDs [package=fkit-led-1206]
  12V_3 = LEDs [package=fkit-led-1206]
  12V_4 = LEDs [package=fkit-led-1206]
  12V_5 = LEDs [package=fkit-led-1206]
  12V_6 = LEDs [package=fkit-led-1206]
  Parte2 = Arduino Board Ethernet  # not connected
  S1 = Pushbutton [package="[THT]"]
  S2 = Pushbutton [package="[THT]"]
  S3 = Pushbutton [package="[THT]"]
  S4 = Pushbutton [package="[THT]"]
  T1 = LM35 Temperature Sensor [package="TO92 [THT]"]
  R1 = Resistor [tolerance=±5% resistance=1k package=THT]
  R2 = Resistor [tolerance=±5% resistance=1k package=THT]
  R4 = Resistor [tolerance=±5% resistance=1k package=THT]
  R3 = Resistor [tolerance=±5% resistance=1k package=THT]

nets:
  N1: Parte1.A15, T1.Vout
  N2: Parte1.D22, IC1.In_1
  N3: Parte1.D23, IC1.In_2
  N4: Parte1.D24, IC1.In_3
  N5: Parte1.D25, IC1.In_4
  N6: Parte1.D26, IC1.In_5
  N7: Parte1.D27, IC1.In_6
  N8: Parte1.D38, S1.Pin_1, S1.Pin_2, R1.Pin_0
  N9: Parte1.D39, S2.Pin_1, S2.Pin_2, R2.Pin_0
  N10: Parte1.D40, S3.Pin_1, S3.Pin_2, R3.Pin_0
  N11: Parte1.D41, S4.Pin_1, S4.Pin_2, R4.Pin_0
  GND: Parte1.GND, IC1.0V, 12V_External_Source.GND, T1.GND, R1.Pin_1, R2.Pin_1, R4.Pin_1, R3.Pin_1
  N12: IC1.Out_6, 12V_5.C
  N13: IC1.Out_5, 12V_6.C
  N14: IC1.Out_4, 12V_4.C
  N15: IC1.Out_3, 12V_3.C
  N16: IC1.Out_2, 12V_2.C
  N17: IC1.Out_1, 12V.C
  N18: 12V_External_Source.VCC, 12V.A, 12V_2.A, 12V_3.A, 12V_4.A, 12V_5.A, 12V_6.A
  5V: S1.Pin_3, S1.Pin_4, S2.Pin_3, S2.Pin_4, S3.Pin_3, S3.Pin_4, S4.Pin_3, T1.+Vs

notes:
  12V external source
